// Logisim project lastname_firstname.circ as structural Verilog
module main (
  input  in_1,
  input  in_2,
  input  in_3,
  input  in_4
);

  wire A_EX, A_MEM, A_WB, and_5_out, and_6_out, and_7_out, and_8_out, and_16_out, and_17_out, B_EX, B_MEM,
       B_WB, BEQ_Equal_bit, CLK, comparator_1_eq, comparator_2_eq, comparator_3_eq, comparator_4_eq,
       comparator_5_eq, comparator_6_eq, comparator_7_eq, comparator_8_eq, comparator_9_eq, comparator_17_eq,
       comparator_18_eq, comparator_19_eq, comparator_20_eq, comparator_21_eq, comparator_22_gt,
       comparator_22_lt, comparator_23_eq, comparator_24_eq, comparator_27_eq, comparator_28_eq,
       comparator_29_eq, EX_NO_FW, Is_JALR, MEM_NO_FW, not_4_out, not_5_out, not_6_out, not_7_out, not_8_out,
       not_9_out, not_10_out, not_11_out, not_12_out, not_13_out, not_14_out, not_15_out, or_1_out, or_2_out,
       or_3_out, or_4_out, or_5_out, WB_NO_FW, WrEn;
  wire [1:0] func;
  wire [2:0] comparator_25_eq, MUX_A;
  wire [2:1] and_3_out, MUX_B;
  wire [3:0] DESTINATION, EX_OP, FW_EX_dest, FW_MEM_dest, FW_MEM_OP, FW_WB_OP, ID_OP, ID_Rx_Code, ID_Ry_Code,
       multiplexer_2_out, Reg_X_or_Z;
  wire [19:0] ID_Off;
  wire [23:0] bit_extender_1_out, bit_extender_3_out;
  wire [31:0] A, adder_1_out, adder_2_out, adder_3_out, adder_5_out, Address, ALU_result, and_15_out, AT, B,
       BEQ_PC, bit_extender_2_out, DataToWrite, EX_Off, EX_PC_q, EX_Signed_Off, FW_EX, FW_LD_MEM, FW_MEM,
       FW_Val_A, FW_Val_B, ID_PC_q, LEA, LEA_q, Loaded_data, multiplexer_1_out, multiplexer_3_out,
       not_16_out, Out_B, PC_q, rom_1_data, Shift_Result;

  Register #(.width(32)) PC (.D(multiplexer_1_out), .Q(PC_q), .clk(CLK), .clr(in_2));  // open: en
  Bit_Extender #(.in_width(32), .out_width(24)) bit_extender_1 (.in(PC_q), .out(bit_extender_1_out));
  Adder #(.width(32)) adder_1 (.a(32'h1), .b(PC_q), .out(adder_1_out));  // open: cin, cout
  Clock clock_1 (.out(CLK));
  Comparator #(.width(4)) comparator_1 (.a(EX_OP), .b(4'b0011), .eq(comparator_1_eq));  // open: gt, lt
  Comparator #(.width(4)) comparator_2 (.a(EX_OP), .b(4'b0111), .eq(comparator_2_eq));  // open: gt, lt
  Comparator #(.width(4)) comparator_3 (.a(EX_OP), .b(4'b1001), .eq(comparator_3_eq));  // open: gt, lt
  Multiplexer #(.select(2), .width(32)) multiplexer_1 (
    .in0(adder_1_out), .in1(AT), .in2(BEQ_PC), .out(multiplexer_1_out), .sel({BEQ_Equal_bit, Is_JALR}));  // open: in3, en
  ROM #(.addrWidth(24), .dataWidth(32)) rom_1 (.addr(bit_extender_1_out), .data(rom_1_data));  // open: sel
  or or_1 (or_1_out, comparator_1_eq, comparator_2_eq, comparator_3_eq);
  Comparator #(.width(4)) comparator_4 (.a(FW_MEM_OP), .b(4'b0011), .eq(comparator_4_eq));  // open: gt, lt
  Comparator #(.width(4)) comparator_5 (.a(FW_MEM_OP), .b(4'b0111), .eq(comparator_5_eq));  // open: gt, lt
  Comparator #(.width(4)) comparator_6 (.a(FW_MEM_OP), .b(4'b1001), .eq(comparator_6_eq));  // open: gt, lt
  Comparator #(.width(4)) comparator_7 (.a(FW_WB_OP), .b(4'b0011), .eq(comparator_7_eq));  // open: gt, lt
  Comparator #(.width(4)) comparator_8 (.a(FW_WB_OP), .b(4'b0111), .eq(comparator_8_eq));  // open: gt, lt
  Comparator #(.width(4)) comparator_9 (.a(FW_WB_OP), .b(4'b1001), .eq(comparator_9_eq));  // open: gt, lt
  Register #(.width(32)) Instruction_Reg (
    .D(rom_1_data), .en(1'b1), .Q({ID_OP, ID_Rx_Code, ID_Ry_Code, ID_Off}), .clk(CLK), .clr(Is_JALR));
  Register #(.width(32)) ID_PC (.D(PC_q), .Q(ID_PC_q), .clk(CLK));  // open: en, clr
  not not_1 (EX_NO_FW, or_1_out);
  or or_2 (or_2_out, comparator_4_eq, comparator_5_eq, comparator_6_eq);
  Comparator #(.width(4)) comparator_10 (.a(ID_Off[3:0]), .b(FW_EX_dest), .eq(B_EX));  // open: gt, lt
  Comparator #(.width(4)) comparator_11 (.a(ID_Off[3:0]), .b(FW_MEM_dest), .eq(B_MEM));  // open: gt, lt
  Comparator #(.width(4)) comparator_12 (.a(ID_Off[3:0]), .b(DESTINATION), .eq(B_WB));  // open: gt, lt
  Comparator #(.width(4)) comparator_13 (.a(ID_Ry_Code), .b(FW_EX_dest), .eq(A_EX));  // open: gt, lt
  Comparator #(.width(4)) comparator_14 (.a(ID_Ry_Code), .b(FW_MEM_dest), .eq(A_MEM));  // open: gt, lt
  Comparator #(.width(4)) comparator_15 (.a(ID_Ry_Code), .b(DESTINATION), .eq(A_WB));  // open: gt, lt
  not not_2 (MEM_NO_FW, or_2_out);
  not not_3 (WB_NO_FW, or_3_out);
  or or_3 (or_3_out, comparator_7_eq, comparator_8_eq, comparator_9_eq);
  not not_4 (not_4_out, B_EX);
  not not_5 (not_5_out, B_EX);
  not not_6 (not_6_out, B_MEM);
  not not_7 (not_7_out, A_EX);
  not not_8 (not_8_out, A_EX);
  not not_9 (not_9_out, A_MEM);
  Adder #(.width(32)) adder_2 (.a(32'h1), .b(ID_PC_q), .out(adder_2_out));  // open: cin, cout
  and and_1 (MUX_B[1], not_4_out, B_MEM);
  and and_2 (MUX_B[2], not_5_out, not_6_out, B_WB);
  and and_3 (and_3_out[1], not_7_out, A_MEM);
  and and_4 (and_3_out[2], not_8_out, not_9_out, A_WB);
  not not_10 (not_10_out, A_EX);
  not not_11 (not_11_out, A_EX);
  not not_12 (not_12_out, A_MEM);
  not not_13 (not_13_out, B_EX);
  not not_14 (not_14_out, B_EX);
  not not_15 (not_15_out, B_MEM);
  and and_5 (and_5_out, not_10_out, A_MEM);
  and and_6 (and_6_out, not_11_out, not_12_out, A_WB);
  and and_7 (and_7_out, not_13_out, B_MEM);
  and and_8 (and_8_out, not_14_out, not_15_out, B_WB);
  Multiplexer #(.width(4)) multiplexer_2 (
    .in0(DESTINATION), .in1(4'b1111), .out(multiplexer_2_out), .sel(Is_JALR));  // open: en
  Multiplexer #(.width(32)) multiplexer_3 (
    .in0(DataToWrite), .in1(adder_2_out), .out(multiplexer_3_out), .sel(Is_JALR));  // open: en
  Comparator #(.width(4)) comparator_16 (.a(ID_OP), .b(4'b0100), .eq(Is_JALR));  // open: gt, lt
  and and_9 (MUX_A[0], A_EX, EX_NO_FW);
  and and_10 (B_EX, B_EX, EX_NO_FW);
  and and_11 (MUX_A[1], and_5_out, MEM_NO_FW);
  and and_12 (MUX_A[2], and_6_out, WB_NO_FW);
  and and_13 (MUX_B[1], and_7_out, MEM_NO_FW);
  and and_14 (MUX_B[2], and_8_out, WB_NO_FW);
  Multiplexer #(.select(3), .width(32)) multiplexer_4 (
    .in0(Out_B), .in1(FW_EX), .in2(FW_MEM), .in4(DataToWrite), .out(FW_Val_B), .sel({MUX_B, B_EX}));  // open: in3, in5, in6, in7, en
  Dual_Ported_Register_File dual_ported_register_file_1 (
    .CLK(CLK), .WrREGNO(multiplexer_2_out), .RdREGNO1(ID_Ry_Code), .RdREGNO2(Reg_X_or_Z),
    .INPUT(multiplexer_3_out), .OUT1(AT), .OUT2(Out_B), .WrEN(WrEn));
  Multiplexer #(.select(3), .width(32)) multiplexer_5 (
    .in0(AT), .in1(FW_EX), .in2(FW_MEM), .in4(DataToWrite), .out(FW_Val_A), .sel(MUX_A));  // open: in3, in5, in6, in7, en
  assign bit_extender_2_out = {{12{1'b0}}, ID_Off};  // Bit_Extender bit_extender_2
  Register #(.width(32)) register_1 (
    .D({{13{ID_Off[19]}}, ID_Off[18:0]}), .Q(EX_Signed_Off), .clk(CLK));  // open: en, clr
  Register #(.width(32)) register_2 (.D(bit_extender_2_out), .Q(EX_Off), .clk(CLK));  // open: en, clr
  Register #(.width(4)) register_3 (.D(ID_Rx_Code), .Q(FW_EX_dest), .clk(CLK));  // open: en, clr
  Register #(.width(32)) Reg_A (.D(FW_Val_A), .Q(B), .clk(CLK));  // open: en, clr
  Register #(.width(32)) Reg_B (.D(FW_Val_B), .Q(A), .clk(CLK));  // open: en, clr
  Register #(.width(4)) u_EX_OP (.D(ID_OP), .Q(EX_OP), .clk(CLK));  // open: en, clr
  Register #(.width(32)) EX_PC (.D(ID_PC_q), .Q(EX_PC_q), .clk(CLK));  // open: en, clr
  Comparator #(.width(32)) comparator_17 (.a(A), .b(B), .eq(comparator_17_eq));  // open: gt, lt
  Comparator #(.width(4)) comparator_18 (.a(EX_OP), .b(4'b1000), .eq(comparator_18_eq));  // open: gt, lt
  Comparator #(.width(4)) comparator_19 (.a(ID_OP), .b(4'b1001), .eq(comparator_19_eq));  // open: gt, lt
  Comparator #(.width(4)) comparator_20 (.a(ID_OP), .b(4'b0011), .eq(comparator_20_eq));  // open: gt, lt
  Adder #(.width(32)) adder_3 (.a(B), .b(A), .out(adder_3_out));  // open: cin, cout
  assign and_15_out = A & B;  // AND_Gate and_15, 32 bits wide
  Adder #(.width(32)) adder_4 (.a(EX_PC_q), .b(EX_Signed_Off), .out(BEQ_PC));  // open: cin, cout
  Adder #(.width(32)) adder_5 (.a(B), .b(EX_Off), .out(adder_5_out));  // open: cin, cout
  assign not_16_out = ~and_15_out;  // NOT_Gate not_16, 32 bits wide
  Comparator #(.width(4)) comparator_21 (.a(EX_OP), .b(4'b0011), .eq(comparator_21_eq));  // open: gt, lt
  Multiplexer #(.width(2)) multiplexer_6 (
    .in0(EX_OP[1:0]), .in1(2'b11), .out(func), .sel(comparator_18_eq));  // open: en
  or or_4 (or_4_out, comparator_19_eq, comparator_20_eq);
  and and_16 (and_16_out, comparator_17_eq, comparator_21_eq);
  Multiplexer #(.width(4)) multiplexer_7 (
    .in0(ID_Off[3:0]), .in1(ID_Rx_Code), .out(Reg_X_or_Z), .sel(or_4_out));  // open: en
  Multiplexer #(.select(2), .width(32)) multiplexer_8 (
    .in0(adder_3_out), .in1(adder_5_out), .in2(not_16_out), .in3(Shift_Result), .out(FW_EX), .sel(func));  // open: en
  Register #(.width(4)) Destination_reg (.D(FW_EX_dest), .Q(FW_MEM_dest), .clk(CLK));  // open: en, clr
  Register #(.width(32)) EX_Result (.D(FW_EX), .Q(FW_MEM), .clk(CLK));  // open: en, clr
  Register #(.width(4)) register_4 (.D(EX_OP), .Q(FW_MEM_OP), .clk(CLK));  // open: en, clr
  Register #(.width(32)) LDR_Addr (.D(adder_5_out), .Q(Address), .clk(CLK));  // open: en, clr
  Register #(.width(32)) u_LEA (.D(BEQ_PC), .Q(LEA_q), .clk(CLK));  // open: en, clr
  Comparator #(.width(32)) comparator_22 (.a(A), .b(B), .gt(comparator_22_gt), .lt(comparator_22_lt));  // open: eq
  Bit_Extender #(.in_width(32), .out_width(24)) bit_extender_3 (.in(Address), .out(bit_extender_3_out));
  or or_5 (or_5_out, comparator_22_gt, comparator_22_lt);
  Comparator #(.width(4)) comparator_23 (.a(EX_OP), .b(4'b1001), .eq(comparator_23_eq));  // open: gt, lt
  or or_6 (BEQ_Equal_bit, and_16_out, and_17_out);
  and and_17 (and_17_out, or_5_out, comparator_23_eq);
  Comparator #(.width(4)) comparator_24 (.a(FW_MEM_OP), .b(4'b0111), .eq(comparator_24_eq));  // open: gt, lt
  RAM #(.addrWidth(24), .dataWidth(32), .bus("separate")) ram_1 (
    .addr(bit_extender_3_out), .din(FW_MEM), .data(FW_LD_MEM), .str(comparator_24_eq), .clk(CLK), .ld(in_1),
    .clr(in_3));  // open: sel
  Register #(.width(4)) WB_Dest_reg (.D(FW_MEM_dest), .Q(DESTINATION), .clk(CLK));  // open: en, clr
  Register #(.width(32)) u_Loaded_Data (.D(FW_LD_MEM), .Q(Loaded_data), .clk(CLK));  // open: en, clr
  Register #(.width(4)) WB_OP (.D(FW_MEM_OP), .Q(FW_WB_OP), .clk(CLK));  // open: en, clr
  Register #(.width(32)) u_ALU_result (.D(FW_MEM), .Q(ALU_result), .clk(CLK));  // open: en, clr
  Register #(.width(32)) LEA_2 (.D(LEA_q), .Q(LEA), .clk(CLK));  // open: en, clr
  Comparator #(.width(4)) comparator_25 (.a(FW_WB_OP), .b(4'b0110), .eq(comparator_25_eq[0]));  // open: gt, lt
  Comparator #(.width(4)) comparator_26 (.a(FW_WB_OP), .b(4'b0101), .eq(comparator_25_eq[1]));  // open: gt, lt
  Comparator #(.width(4)) comparator_27 (.a(FW_WB_OP), .b(4'b0000), .eq(comparator_27_eq));  // open: gt, lt
  Comparator #(.width(4)) comparator_28 (.a(FW_WB_OP), .b(4'b0001), .eq(comparator_28_eq));  // open: gt, lt
  Comparator #(.width(4)) comparator_29 (.a(FW_WB_OP), .b(4'b0010), .eq(comparator_29_eq));  // open: gt, lt
  or or_7 (comparator_25_eq[2], comparator_27_eq, comparator_28_eq, comparator_29_eq);
  or or_8 (WrEn, comparator_25_eq[2], comparator_25_eq[1], comparator_25_eq[0]);
  Multiplexer #(.select(3), .width(32)) multiplexer_9 (
    .in1(LEA), .in2(Loaded_data), .in4(ALU_result), .out(DataToWrite), .sel(comparator_25_eq));  // open: in0, in3, in5, in6, in7, en

  // Other names for the same wires on the sheet: FW_EX_OP[3:0] = EX_OP; FW_WB[31:0] = DataToWrite;
  //   FW_WB_dest[3:0] = DESTINATION; MEM_OP[3:0] = FW_MEM_OP; MUX_B[0] = B_EX; ID_Rz_Code[3:0] = ID_Off[3:0];
  //   off_split[31:0] = {{13{ID_Off[19]}}, ID_Off[18:0]}; Out_A[31:0] = AT; RST = in_4

  // Notes on the sheet:
  //   contents of rom_1 (hex, n*v repeats v):
  //   3000000 4000000 1440000a 13300001 73300000 7330000a 934ffffd
  //   BEQ/BNE Unit
endmodule

module Dual_Ported_Register_File (
  input  CLK,
  input  WrEN,
  input  [3:0] WrREGNO,
  input  [3:0] RdREGNO1,
  input  [3:0] RdREGNO2,
  input  [31:0] INPUT,
  output [31:0] OUT1,
  output [31:0] OUT2
);

  wire En_a0, En_a1, En_a2, En_at, En_fp, En_k0, En_ra, En_s0, En_s1, En_s2, En_sp, En_t0, En_t1, En_t2,
       En_v0;
  wire [31:0] a0, a1, a2, at, fp, k0, ra, s0, s1, s2, sp, t0, t1, t2, v0, zero;

  Decoder #(.select(4), .disabled(0)) decoder_1 (
    .out1(En_at), .out2(En_v0), .out3(En_a0), .out4(En_a1), .out5(En_a2), .out6(En_t0), .out7(En_t1),
    .out8(En_t2), .out9(En_s0), .out10(En_s1), .out11(En_s2), .out12(En_k0), .out13(En_sp), .out14(En_fp),
    .out15(En_ra), .sel(WrREGNO), .en(WrEN));  // open: out0
  Register #(.width(32)) u_zero (.D(INPUT), .en(1'b0), .Q(zero), .clk(CLK));  // open: clr
  Register #(.width(32)) u_at (.D(INPUT), .en(En_at), .Q(at), .clk(CLK));  // open: clr
  Register #(.width(32)) u_v0 (.D(INPUT), .en(En_v0), .Q(v0), .clk(CLK));  // open: clr
  Register #(.width(32)) u_a0 (.D(INPUT), .en(En_a0), .Q(a0), .clk(CLK));  // open: clr
  Register #(.width(32)) u_a1 (.D(INPUT), .en(En_a1), .Q(a1), .clk(CLK));  // open: clr
  Register #(.width(32)) u_a2 (.D(INPUT), .en(En_a2), .Q(a2), .clk(CLK));  // open: clr
  Register #(.width(32)) u_t0 (.D(INPUT), .en(En_t0), .Q(t0), .clk(CLK));  // open: clr
  Register #(.width(32)) u_t1 (.D(INPUT), .en(En_t1), .Q(t1), .clk(CLK));  // open: clr
  Multiplexer #(.select(4), .width(32), .disabled(0), .enable("false")) multiplexer_1 (
    .in0(zero), .in1(at), .in2(v0), .in3(a0), .in4(a1), .in5(a2), .in6(t0), .in7(t1), .in8(t2), .in9(s0),
    .in10(s1), .in11(s2), .in12(k0), .in13(sp), .in14(fp), .in15(ra), .out(OUT2), .sel(RdREGNO2));
  Register #(.width(32)) u_t2 (.D(INPUT), .en(En_t2), .Q(t2), .clk(CLK));  // open: clr
  Register #(.width(32)) u_s0 (.D(INPUT), .en(En_s0), .Q(s0), .clk(CLK));  // open: clr
  Register #(.width(32)) u_s1 (.D(INPUT), .en(En_s1), .Q(s1), .clk(CLK));  // open: clr
  Register #(.width(32)) u_s2 (.D(INPUT), .en(En_s2), .Q(s2), .clk(CLK));  // open: clr
  Register #(.width(32)) u_k0 (.D(INPUT), .en(En_k0), .Q(k0), .clk(CLK));  // open: clr
  Register #(.width(32)) u_sp (.D(INPUT), .en(En_sp), .Q(sp), .clk(CLK));  // open: clr
  Register #(.width(32)) u_fp (.D(INPUT), .en(En_fp), .Q(fp), .clk(CLK));  // open: clr
  Register #(.width(32)) u_ra (.D(INPUT), .en(En_ra), .Q(ra), .clk(CLK));  // open: clr
  Multiplexer #(.select(4), .width(32), .disabled(0), .enable("false")) multiplexer_2 (
    .in0(zero), .in1(at), .in2(v0), .in3(a0), .in4(a1), .in5(a2), .in6(t0), .in7(t1), .in8(t2), .in9(s0),
    .in10(s1), .in11(s2), .in12(k0), .in13(sp), .in14(fp), .in15(ra), .out(OUT1), .sel(RdREGNO1));

  // Notes on the sheet:
  //   MODIFY AT YOUR OWN RISK
endmodule
